# Fritzing sketch Bubble Wall (saved by Fritzing 0.9.3b)

parts:
  Part1 = Arduino Mega 2560 (Rev3)
  JACK1 = 2.1mm Barrel Jack with Terminal Block
  Q1 = TIP120 Hi-Current Darlington Transistor
  R1 = Resistor [tolerance=±5% resistance=10k package=THT]
  D1 = Rectifier Diode [part_number=1N4001 package="300 mil [THT]"]
  M1 = DC Motor
  Q2 = TIP120 Hi-Current Darlington Transistor
  R2 = Resistor [tolerance=±5% resistance=10k package=THT]
  D2 = Rectifier Diode [part_number=1N4001 package="300 mil [THT]"]
  M2 = DC Motor
  Q3 = TIP120 Hi-Current Darlington Transistor
  R3 = Resistor [tolerance=±5% resistance=10k package=THT]
  D3 = Rectifier Diode [part_number=1N4001 package="300 mil [THT]"]
  M3 = DC Motor
  Q4 = TIP120 Hi-Current Darlington Transistor
  R4 = Resistor [tolerance=±5% resistance=10k package=THT]
  D4 = Rectifier Diode [part_number=1N4001 package="300 mil [THT]"]
  M4 = DC Motor
  Q5 = TIP120 Hi-Current Darlington Transistor
  R5 = Resistor [tolerance=±5% resistance=10k package=THT]
  D5 = Rectifier Diode [part_number=1N4001 package="300 mil [THT]"]
  M5 = DC Motor

nets:
  N1: Part1.D17_PWM/RX2, R5.Pin_0
  N2: Part1.D16_PWM/TX2, R4.Pin_0
  N3: Part1.D15/RX3, R3.Pin_0
  N4: Part1.D14/TX3, R2.Pin_0
  N5: Part1.GND, JACK1.NEG, Q1.EMITTER, Q2.EMITTER, Q3.EMITTER, Q4.EMITTER, Q5.EMITTER
  N6: Part1.D13_PWM, R1.Pin_0
  N7: JACK1.POS, D1.cathode, M1.pin_1, D2.cathode, M2.pin_1, D3.cathode, M3.pin_1, D4.cathode, M4.pin_1, D5.cathode, M5.pin_1
  N8: Q1.BASE, R1.Pin_1
  N9: Q1.COLLECTOR, D1.anode, M1.pin_2
  N10: Q2.BASE, R2.Pin_1
  N11: Q2.COLLECTOR, D2.anode, M2.pin_2
  N12: Q3.BASE, R3.Pin_1
  N13: Q3.COLLECTOR, D3.anode, M3.pin_2
  N14: Q4.BASE, R4.Pin_1
  N15: Q4.COLLECTOR, D4.anode, M4.pin_2
  N16: Q5.BASE, R5.Pin_1
  N17: Q5.COLLECTOR, D5.anode, M5.pin_2

notes:
  3V DC Regulated
  SC3101PM Micro Vaccum Pump
